# Fritzing sketch circuit (saved by Fritzing 0.9.3b)
breadboards: 1

parts:
  J4 = Basic Servo
  VCC1 = Battery
  VCC2 = Battery
  Raspberry_Pi_1 = Raspberry Pi 3 [part_number=RPI-3-V1.2]
  J1 = Basic Servo
  J3 = Basic Servo
  J2 = Basic Servo
  U1 = LIPO-1000mAh [package=lipo-1000]  # not connected
  U2 = TRANSCHIPTC5747 [package=camera_sfv24r-2st_2]
  CONN1 = USB connector [package=THT]

nets:
  GND: J4.gnd, VCC2.-, Raspberry_Pi_1.GND, J1.gnd, J3.gnd, J2.gnd
  VCC: J4.vcc, VCC1.+, J1.vcc, J3.vcc, J2.vcc
  N1: J4.pulse, Raspberry_Pi_1.GPIO25
  N2: VCC1.-, VCC2.+
  N3: Raspberry_Pi_1.GPIO12, J1.pulse
  N4: Raspberry_Pi_1.GPIO7, J2.pulse
  N5: Raspberry_Pi_1.GPIO8, J3.pulse
  N6: U2.SCLK, CONN1.d-
  N7: U2.AGND, CONN1.d+
  N8: U2.AVDD28, CONN1.chassis5
  N9: U2.RESET_N, CONN1.5V

notes:
  Servo Motor Power Supply
  End Effector Servo
  Servos for joints 1, 2, and 3
  Raspberry Pi Power Supply
  USB Camera
